# Fritzing sketch circuito (saved by Fritzing 0.9.9b)
breadboards: 2

parts:
  Componente1 = Arduino Uno (Rev3) - ICSP  # not connected
  Componente2 = Arduino Uno (Rev3) - ICSP  # not connected
  S1 = Pushbutton [package="[THT]"]
  S2 = Pushbutton [package="[THT]"]
  S3 = Pushbutton [package="[THT]"]
  S4 = Pushbutton [package="[THT]"]
  R1 = Resistor [tolerance=±5% power=0.25 resistance=220 package=THT]
  LED1 = smd LED [color="Red (633nm)" package="0603 [SMD]"]
  LED2 = smd LED [color="Orange (620nm)" package="0603 [SMD]"]
  R2 = Resistor [tolerance=±5% power=0.25 resistance=220 package=THT]
  R3 = Resistor [tolerance=±5% power=0.25 resistance=220 package=THT]
  LED3 = smd LED [color="Red (633nm)" package="0603 [SMD]"]
  U1 = RF-LINK_TX [package=rf-link_tx]  # not connected
  U2 = RF-LINK_RX [package=rf-link_rx]  # not connected

nets:
  N1: S1.Pin_1, S1.Pin_2
  N2: S1.Pin_3, S1.Pin_4
  N3: S2.Pin_1, S2.Pin_2
  N4: S2.Pin_3, S2.Pin_4, R3.Pin_1
  N5: S3.Pin_1, S3.Pin_2
  N6: S3.Pin_3, S3.Pin_4, R1.Pin_1
  N7: S4.Pin_1, S4.Pin_2
  N8: S4.Pin_3, S4.Pin_4, R2.Pin_1
  N9: R1.Pin_0, LED2.anode
  N10: LED1.cathode, LED2.cathode, LED3.cathode
  N11: LED1.anode, R2.Pin_0
  N12: R3.Pin_0, LED3.anode
